# Fritzing sketch Finn (saved by Fritzing 0.9.3b)
breadboards: 1

parts:
  Part1 = Arduino Mega ADK (Rev3)
  R1 = Resistor [tolerance=±5% resistance=10k package="0603 [SMD]"]
  LED1 = smd LED [color="White (4500K)" package="1206 [SMD]"]
  T1 = TMP36 Temperature Sensor [package="TO92 [THT]"]
  J1 = Basic Servo

nets:
  N1: Part1.A1, T1.Vout
  N2: Part1.D21/SCL, R1.Pin_1
  N3: Part1.D9_PWM, J1.pulse
  5V: Part1.5V, T1.+Vs, J1.vcc
  GND: Part1.GND, LED1.cathode, T1.GND, J1.gnd
  N4: R1.Pin_0, LED1.anode
